# Fritzing sketch Sunshine (saved by Fritzing 0.9.3b)
breadboards: 1

parts:
  U1 = ESP8266 WiFi Module [part_number=ESP8266]
  Q1 = MOSFET-NCHANNEL [part_number=2N7000 package=to-92]
  LED1 = LED - 3mm [color="Red (633nm)" package="3 mm [THT]"]
  U2 = V_REG_LD1117VXX [package=78xxl]
  Power_plug1 = Power plug
  元件1 = FTDI Basic Programmer
  S1 = Momentary Switch [package=ksa_sealed_tac_switch]
  S3 = Toggle Switch [package=THT]
  C1 = Capacitor Polarized [package=cpol-radial-1000uf-25v]
  C2 = Electrolytic Capacitor [capacitance=1000μF package="1010 [SMD, electrolytic]"]
  C3 = Capacitor [package=cap-pth-small2]
  C4 = Capacitor [package=cap-pth-small2]

nets:
  N1: U1.RXD, 元件1.TXO
  N2: U1.VCC, U1.CH_PD, U2.IN, C2.+, C4.1
  N3: U1.GPIO_0, S1.3
  N4: U1.GPIO_2, Q1.S
  GND: U1.GND, Q1.G, U2.OUT, Power_plug1.GND, 元件1.GND, S1.2, C2.-, C4.2
  N5: U1.TXD, 元件1.RXI
  N6: Q1.D, LED1.cathode
  N7: LED1.anode, U2.GND, S3.L2, C1.+, C3.1
  N8: Power_plug1.VCC, S3.COM
  N9: C1.-, C3.2

custom parts:
  ESP8266 WiFi Module: Generic WiFi Module based on the ESP8266 with onboard PCB antenna and UART communications
